# Fritzing sketch arduino_prototype (saved by Fritzing 0.9.3b)
breadboards: 1

parts:
  M1 = DC Motor
  M2 = DC Motor
  IC1 = L293D [package=THT]
  MotorPower = Battery Holders [package=battery-aa-kit]
  U1 = NodeMCU V1.0
  5v = Battery Holders [package=battery-aa-kit]

nets:
  N1: M1.pin_1, IC1.Out_4_(_Controlled_by_Enable_2_)
  N2: M1.pin_2, IC1.Out_3_(_Controlled_by_Enable_2_)
  N3: M2.pin_1, IC1.Out_2_(_Controlled_by_Enable_1_)
  N4: M2.pin_2, IC1.Out_1_(_Controlled_by_Enable_1_)
  N5: IC1.In_1, U1.D5
  N6: IC1.0V, MotorPower.-, U1.GND, 5v.+, 5v.-
  N7: IC1.In_2, U1.D6
  N8: IC1.+Vmotor, MotorPower.+
  N9: IC1.In_3, U1.D2
  N10: IC1.In_4, U1.D1

custom parts:
  NodeMCU V1.0: ESP8266 based NodeMCU
