# Fritzing sketch esp32cam+led+button+servo+flash (saved by Fritzing 0.9.9b)
circuit board: 8.46667cm x 5.64444cm
breadboards: 1

parts:
  LED1 = LEDs [package=led10mm]
  LED2 = LEDs [package=led10mm]
  LED3 = LEDs [package=led10mm]
  LED4 = LEDs [package=led10mm]
  LED5 = LEDs [package=led10mm]
  S3 = Momentary Switch [package=ksa_sealed_tac_switch]
  IC1 = L293D [package=THT]
  M2 = DC Motor
  M3 = DC Motor
  ESP32_-_Back1 = ESP32 - CAM

nets:
  N1: LED1.A, ESP32_-_Back1.GPIO14
  N2: LED2.A, ESP32_-_Back1.GPIO13
  N3: LED3.A, ESP32_-_Back1.GPIO2
  N4: LED4.A, ESP32_-_Back1.GPIO15
  N5: LED5.A, S3.3, ESP32_-_Back1.GPIO12, ESP32_-_Back1.GND#16
  N6: S3.2, S3.4
  N7: IC1.In_1, IC1.In_2, IC1.In_3, IC1.In_4, ESP32_-_Back1.GPIO16
  N8: IC1.Out_1_(_Controlled_by_Enable_1_), M3.pin_2
  N9: IC1.Out_2_(_Controlled_by_Enable_1_), M3.pin_1
  N10: IC1.Out_3_(_Controlled_by_Enable_2_), M2.pin_2
  N11: IC1.Out_4_(_Controlled_by_Enable_2_), M2.pin_1

custom parts:
  ESP32 - CAM: The ESP32-CAM has a very competitive small-size camera module that can operate independently as a minimum system with a footprint of only 27*40.5*4.5mm and a deep sleep current of up to 6mA.
